# Fritzing sketch Psismos_Schematics (saved by Fritzing 1.0.6)
breadboards: 2

parts:
  Pressure_Sensor = Adafruit MPRLS Sensor Breakout [part_number=3965]
  Amplifier_Board = Adafruit MAX9744 20W Amplifier [part_number="Adafruit #1752"]
  12V/3A_Power_Supply = DC Power [voltage=12V internal_resistance=0.1Ω]
  R4 = Resistor [tolerance=±5% power=0.25W resistance=2.2k package=THT]
  R5 = Resistor [tolerance=±5% power=0.25W resistance=2.2k package=THT]
  A1 = Raspberry Pi Pico2
  DAC = Adafruit PCM510x I2S DAC [part_number=#6250]
  3_7_V_LiPo_Battery = LIPO-1000mAh [package=lipo-1000]
  Motion_Sensor = InvenSense MPU6050
  SPKR1 = Loudspeaker

nets (from the schematic view):
  VIN: Pressure_Sensor.VIN, A1.pin_36, DAC.VIN, Motion_Sensor.VCC
  GND: Pressure_Sensor.GND, A1.pin_3, A1.pin_8, A1.pin_13, A1.pin_18, A1.pin_23, A1.pin_28, A1.pin_33, A1.pin_38, DAC.AGND, 3_7_V_LiPo_Battery.-, Motion_Sensor.GND
  N1: Pressure_Sensor.SCL, R4.Pin_1, Motion_Sensor.SCL
  N2: Pressure_Sensor.SDA, R5.Pin_1, Motion_Sensor.SDA
  N3: Amplifier_Board.PWRIN, 12V/3A_Power_Supply.V+
  N4: Amplifier_Board.RIGHT-, SPKR1.pin1
  N5: Amplifier_Board.RIGHT+, SPKR1.pin2
  N6: Amplifier_Board.RIGHTIN, DAC.OUTR
  N7: Amplifier_Board.LEFTIN, DAC.OUTL
  N8: Amplifier_Board.AGND, 12V/3A_Power_Supply.V-
  N9: R4.Pin_0, A1.pin_22
  N10: R5.Pin_0, A1.pin_21
  N11: A1.pin_14, DAC.BITCLK_IN
  N12: A1.pin_15, DAC.WORDSEL_IN
  N13: A1.pin_16, DAC.DATA_IN
  N14: A1.pin_39, 3_7_V_LiPo_Battery.+

notes:
  Please refer to the schematic view for the correct diagram. For some reason, the breadboard view does not properly reflect the connections made in the schematic view (maybe a problem with the way the fritzing parts were built).
  The actual DAC component for this project was the Freenove Audio Converter and Amplifier. This part has the same chip and capabilities and was easier to access on Fritzing (included in Adafruit's Fritzing library).
  The actual Amplifier component for this project was the MOD-PAM8610-D Audio Amplifier Board. This part has the capabilities and was easier to access on Fritzing (included in Adafruit's Fritzing library).
  Additionally, a transducer is connected to the Left- and Left+ outs of the Amplifier board

custom parts:
  Adafruit MPRLS Sensor Breakout: This pressure sensor is special because it comes with a metal port - you can easily attach a tube to it, to measure air pressure inside a close space. In particular we think this would be a great sensor for use with making DIY assistive tech "Sip & Puff" interfaces, or measuring the pressure within a vacuum chamber or other pressurized container. The port is made of stainless steel and is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
  Adafruit MAX9744 20W Amplifier: Pump up the volume with this 20W stereo amplifier! This slim little board has a class D amplifier onboard that can drive 2 channels of 4-8 ohm impedance speakers at 20W each. Power it with 5-12VDC using the onboard DC power jack and plug stereo line level into the 3.5mm stereo headphone jack and jam out with ease. Since it's class D, its completely cool-running, no heat sinks are required and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
  Raspberry Pi Pico2: Raspberry Pi Pico 2W is our new $7 microcontroller board, built on RP2350: our new high-performance, secure microcontroller with on board WiFi.
  Adafruit PCM510x I2S DAC: We stock a lot of chips and development boards that are able to do high quality digital I2S out, which makes for great quality audio playback. That's great when you have enough processing power to decode WAVs or MP3s in real time. However, we don't have a good selection of I2S DAC boards...until now! We really love the sounds coming out of the Adafruit PCM5102 I2S DAC with Line Level Output -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
