# Fritzing sketch compressionReleaseCircuitDiagram (saved by Fritzing 1.0.6)
breadboards: 1

parts:
  Part1 = Adafruit MPRLS Sensor Breakout [part_number=3965]
  Mod1 = Raspberry Pi Pico W
  R1 = Photocell (LDR) [power=0.25W dark_resistance_@0.01lx=300kΩ light_resistance_@100lx=400Ω luminance=10lx package=THT]
  R2 = Resistor [tolerance=±5% resistance=10k package="2512 [SMD]"]

nets:
  N1: Part1.VIN, Mod1.pin_36, R1.pin_0
  N2: Part1.GND, Mod1.pin_3, Mod1.pin_8, Mod1.pin_13, Mod1.pin_18, Mod1.pin_23, Mod1.pin_28, Mod1.pin_33, Mod1.pin_38, R2.Pin_1
  N3: Part1.SCL, Mod1.pin_17
  N4: Part1.SDA, Mod1.pin_16
  N5: Mod1.pin_31, R1.pin_1, R2.Pin_0

custom parts:
  Adafruit MPRLS Sensor Breakout: This pressure sensor is special because it comes with a metal port - you can easily attach a tube to it, to measure air pressure inside a close space. In particular we think this would be a great sensor for use with making DIY assistive tech "Sip & Puff" interfaces, or measuring the pressure within a vacuum chamber or other pressurized container. The port is made of stainless steel and is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
  Raspberry Pi Pico W: Raspberry Pi Pico W. Based around the RP2040 microcontroller the Pico W is a low cost microcontroller device bringing Raspberry Pi quality, cost, and easy of use to the microcontroller space. The areas marked KEEPOUT in pcb silkscreen should not have traces running through them to avoid shorts on a soldered in module!
